# Fritzing sketch ellipto (saved by Fritzing 0.8.7b)
breadboards: 1

parts:
  S1 = Tilt Switch [package=THT]
  Part1 = Electric Imp April
  R1 = Resistor [tolerance=±5% resistance=500 package=THT]
  R2 = Resistor [tolerance=±5% resistance=220k package=THT]
  R3 = Resistor [tolerance=±5% resistance=470k package=THT]
  LED1 = LED - 5mm [color="Red (633nm)" package="5 mm [THT]"]
  BATT1 = 3xAAA Switchable Battery Pack w/Bare Wire

nets:
  N1: S1.Pin_1, Part1.8
  N2: S1.Pin_2, Part1.1
  N3: Part1.3, R2.Pin_0, R3.Pin_1
  N4: Part1.6, LED1.anode
  N5: Part1.9, R1.Pin_1, R2.Pin_1, BATT1.NEG
  N6: Part1.10, R3.Pin_0, BATT1.POS
  N7: R1.Pin_0, LED1.cathode

custom parts:
  Electric Imp April: Electric Imp Breakout Board with onboard 3.3V regulated power supply
  3xAAA Switchable Battery Pack w/Bare Wire: 3xAAA Switchable Battery Pack w/Bare Wire Connectors
